# Fritzing sketch Shirt Folder 2 (saved by Fritzing 0.7.4b)
breadboards: 1

parts:
  Arduino1 = Arduino
  Power_plug1 = Power plug
  Power_plug2 = Power plug
  Power_plug3 = Power plug
  R1 = Resistor [tolerance=±5% resistance=100 package=THT]
  R2 = Resistor [tolerance=±5% resistance=100 package=THT]
  J1 = Basic Servo
  J2 = Basic Servo
  J3 = Basic Servo
  S1 = Toggle Switch [package=THT]

nets:
  N1: Arduino1.D6, J1.pulse
  N2: Arduino1.D5, J2.pulse
  N3: Arduino1.D4, S1.COM
  N4: Arduino1.D3, J3.pulse
  N5: Arduino1.D2, R1.Pin_0, S1.L2
  GND: Arduino1.GND, Power_plug1.GND, Power_plug2.GND, Power_plug3.GND, R2.Pin_1, J1.gnd, J2.gnd, J3.gnd, S1.L1
  VCC: Power_plug1.VCC, J1.vcc
  VCC_2: Power_plug2.VCC, J2.vcc
  VCC_3: Power_plug3.VCC, J3.vcc
  N6: R1.Pin_1, R2.Pin_0
