# Fritzing sketch Shirt Folder 3 (saved by Fritzing 0.7.4b)
breadboards: 1

parts:
  3_5_6_-_+_3 = female pin header, 6 pins [form="♀ (female)"]
  -1 = Battery
  -2 = Battery
  -3 = Battery
  Pulse1 = Basic Servo
  Pulse2 = Basic Servo
  Pulse3 = Basic Servo
  S1 = Toggle Switch [package=THT]
  100 = Resistor [tolerance=±5% resistance=100 package=THT]
  100_2 = Resistor [tolerance=±5% resistance=100 package=THT]

nets:
  N1: 3_5_6_-_+_3.pin1, Pulse1.pulse
  N2: 3_5_6_-_+_3.pin2, Pulse3.pulse
  N3: 3_5_6_-_+_3.pin3, Pulse2.pulse
  GND: 3_5_6_-_+_3.pin4, -1.-, -2.-, -3.-, Pulse1.gnd, Pulse2.gnd, Pulse3.gnd, S1.L1, 100_2.Pin_1
  N4: 3_5_6_-_+_3.pin5, S1.COM
  N5: 3_5_6_-_+_3.pin6, S1.L2, 100.Pin_0
  N6: -1.+, Pulse2.vcc
  N7: -2.+, Pulse3.vcc
  N8: -3.+, Pulse1.vcc
  N9: 100.Pin_1, 100_2.Pin_0
