# Fritzing sketch Shirt Folder (saved by Fritzing 0.7.5b)
breadboards: 1

parts:
  - = Battery
  Pulse = Basic Servo
  -_2 = Battery
  Pulse_2 = Basic Servo
  Pulse_3 = Basic Servo
  -_3 = Battery
  S = Toggle Switch [package=THT]
  100 = Resistor [tolerance=±5% resistance=100 package=THT]
  100_2 = Resistor [tolerance=±5% resistance=100 package=THT]
  3_5_6_-_+_2 = female pin header, 6 pins [form="♀ (female)"]

nets:
  GND: -.-, Pulse.gnd, -_2.-, Pulse_2.gnd, Pulse_3.gnd, -_3.-, S.L1, 100_2.Pin_1, 3_5_6_-_+_2.pin4
  N1: -.+, Pulse.vcc
  N2: Pulse.pulse, 3_5_6_-_+_2.pin1
  N3: -_2.+, Pulse_2.vcc
  N4: Pulse_2.pulse, 3_5_6_-_+_2.pin2
  N5: Pulse_3.vcc, -_3.+
  N6: Pulse_3.pulse, 3_5_6_-_+_2.pin3
  N7: S.COM, 3_5_6_-_+_2.pin5
  N8: S.L2, 100.Pin_0, 3_5_6_-_+_2.pin6
  N9: 100.Pin_1, 100_2.Pin_0

notes:
  Gnd
  +5
  Output
  +
