# Fritzing sketch Complete Circuit (saved by Fritzing 0.8.0b)
breadboards: 1

parts:
  Servo_1_Power_(6V) = 4 x AAA Battery Mount
  Servo_1_Switch = Pushbutton [package=THT]
  Servo_1 = Basic Servo
  Arduino_Uno = Arduino Uno (Rev3)
  Arduino_Power_Supply = Battery block 9V
  Servo_2_Power_(6V) = 4 x AAA Battery Mount
  S2 = Pushbutton [package=THT]
  Servo_2 = Basic Servo
  Servo_3_Power = 4 x AAA Battery Mount
  Servo_3_Swtich = Pushbutton [package=THT]
  Servo_3 = Basic Servo
  Arduino_Switch = Pushbutton [package=THT]
  Main_Switch = Round Pushbutton

nets:
  GND: Servo_1_Power_(6V).-, Servo_1.gnd, Arduino_Uno.GND, Arduino_Power_Supply.-, Servo_2_Power_(6V).-, Servo_2.gnd, Servo_3_Power.-, Servo_3.gnd
  N1: Servo_1_Power_(6V).+, Servo_1_Switch.leg1
  N2: Servo_1_Switch.leg0, Servo_1.vcc
  N3: Servo_1.pulse, Arduino_Uno.D3_PWM
  N4: Arduino_Uno.5V, Main_Switch.leg0
  N5: Arduino_Uno.D2, Main_Switch.leg1
  N6: Arduino_Uno.D5_PWM, Servo_2.pulse
  N7: Arduino_Uno.D6_PWM, Servo_3.pulse
  N8: Arduino_Uno.VIN, Arduino_Switch.leg0
  N9: Arduino_Power_Supply.+, Arduino_Switch.leg1
  N10: Servo_2_Power_(6V).+, S2.leg1
  N11: S2.leg0, Servo_2.vcc
  N12: Servo_3_Power.+, Servo_3_Swtich.leg1
  N13: Servo_3_Swtich.leg0, Servo_3.vcc
